// Logisim project POS-Updated.circ as structural Verilog: 1 circuit, main circuit main
module main (
  input  A,
  input  B,
  input  C
);

  wire a_t, b_t, c_t, d, e, f, g, not_1_out, not_2_out, not_3_out, or_1_out, or_5_out, or_7_out, or_9_out;

  not not_1 (not_1_out, A);
  not not_2 (not_2_out, C);
  not not_3 (not_3_out, B);
  or or_1 (or_1_out, A, B);
  or or_2 (a_t, not_3_out, not_2_out);
  or or_3 (b_t, not_1_out, B);
  or or_4 (c_t, B, C);
  or or_5 (or_5_out, A, B, not_2_out);
  or or_6 (e, B, not_2_out);
  or or_7 (or_7_out, A, not_2_out);
  or or_8 (g, A, B, not_2_out);
  or or_9 (or_9_out, not_1_out, B, C);
  and and_1 (f, or_1_out, or_7_out);
  _7_Segment_Display u_7_segment_display_1 (.g(g), .f(f), .a(a_t), .b(b_t), .e(e), .d(d), .c(c_t));  // open: dp
  and and_2 (d, or_5_out, or_9_out);
endmodule
